// Digital circuit computer.dig as structural Verilog
module computer (
  input  clk,
  output out_1,
  output out_2,
  output out_3,
  output out_4,
  output out_5,
  output out_6,
  output out_7,
  output out_8,
  output [7:0] out_9,
  output [7:0] out_10,
  output out_11,
  output out_12,
  output out_13,
  output out_14,
  output [7:0] out_15,
  output [7:0] out_16,
  output [7:0] out_17,
  output [1:0] out_18,
  output [7:0] out_19,
  output [7:0] out_20,
  output out_21,
  output out_22,
  output [7:0] out_23,
  output out_24,
  output out_26,
  output out_27,
  output out_28,
  output out_29,
  output out_30,
  output out_31,
  output out_32,
  output [7:0] out_33,
  output [7:0] out_34,
  output out_35
);

  wire and_3_out, and_4_out, and_5_out, and_6_out, and_9_out, and_10_out, and_11_out, and_12_out, and_13_out,
       and_14_out, and_15_out, and_16_out, and_17_out, and_18_out, and_19_out, and_20_out, and_21_out,
       and_22_out, and_23_out, and_24_out, and_25_out, and_26_out, and_27_out, IC_ovf, not_1_out, not_2_out,
       not_3_out, not_5_out, not_6_out, not_7_out, not_8_out, not_9_out, not_10_out, not_11_out, not_12_out,
       not_13_out, not_14_out, not_15_out, not_16_out, not_17_out, not_18_out, not_19_out, not_20_out,
       not_21_out, not_22_out, not_23_out, not_24_out, not_25_out, not_26_out, not_27_out, not_28_out,
       not_29_out, not_30_out, not_31_out, not_32_out, not_33_out, not_34_out, not_35_out, not_36_out,
       or_2_out, OUT, register_2_q, WJMP, WJMPSTORE;
  wire [3:0] rom_2_d_2, rom_3_d_2, rom_4_d_2;
  wire [7:0] _8_bit_adder_s, and_7_out, and_8_out, driver_15_out, FUFLAG, not_4_out, or_1_out, REGOUT_q,
       rom_1_d, rom_2_d, rom_3_d, rom_4_d, xor_1_out;

  Register register_1 (.D(out_31), .C(clk), .en(out_26), .Q(out_31));
  assign out_33 = {8{1'b0}} & out_20;  // And and_1, 8 bits wide
  assign FUFLAG = {8{1'b1}} & out_20;  // And and_2, 8 bits wide
  PullDown pulldown_1 (.out(WJMP));
  not not_1 (not_1_out, out_18[1]);
  not not_2 (not_2_out, out_18[0]);
  Register register_2 (.D(WJMP), .C(clk), .en(WJMPSTORE), .Q(register_2_q));
  PullDown pulldown_2 (.out(WJMPSTORE));
  and and_3 (and_3_out, not_2_out, not_1_out);
  and and_4 (and_4_out, out_18[0], not_1_out);
  and and_5 (and_5_out, out_18[1], not_2_out);
  and and_6 (and_6_out, out_18[0], out_18[1]);
  Add #(.Bits(8)) _8_bit_adder (.a(out_19), .b(out_20), .c_i(1'b0), .s(_8_bit_adder_s), .c_o(out_31));
  assign and_7_out = out_19 & out_20;  // And and_7, 8 bits wide
  assign xor_1_out = out_19 ^ out_20;  // XOr xor_1, 8 bits wide
  assign and_8_out = out_19 & out_20;  // And and_8, 8 bits wide
  and and_9 (and_9_out, and_6_out, register_2_q);
  and and_10 (and_10_out, and_6_out, not_3_out);
  not not_3 (not_3_out, register_2_q);
  assign out_9 = out_35 ? and_8_out : 8'bz;  // Driver driver_1
  assign out_5 = and_3_out ? 1'b1 : 1'bz;  // Driver driver_2
  assign out_14 = and_3_out ? 1'b1 : 1'bz;  // Driver driver_3
  assign out_11 = and_3_out ? 1'b1 : 1'bz;  // Driver driver_4
  assign WJMPSTORE = and_3_out ? 1'b1 : 1'bz;  // Driver driver_5
  assign out_6 = and_4_out ? 1'b1 : 1'bz;  // Driver driver_6
  assign out_14 = and_4_out ? 1'b1 : 1'bz;  // Driver driver_7
  PullDown pulldown_3 (.out(out_26));
  assign out_9 = out_26 ? _8_bit_adder_s : 8'bz;  // Driver driver_8
  PullDown pulldown_4 (.out(out_27));
  assign out_9 = out_27 ? and_7_out : 8'bz;  // Driver driver_9
  PullDown pulldown_5 (.out(out_29));
  assign out_9 = out_29 ? xor_1_out : 8'bz;  // Driver driver_10
  PullDown pulldown_6 (.out(out_35));
  assign out_24 = and_9_out ? 1'b1 : 1'bz;  // Driver driver_11
  assign out_11 = and_10_out ? 1'b1 : 1'bz;  // Driver driver_12
  assign or_1_out = out_19 | out_20;  // Or or_1, 8 bits wide
  assign not_4_out = ~out_19;  // Not not_4, 8 bits wide
  not not_5 (not_5_out, driver_15_out[7]);
  not not_6 (not_6_out, driver_15_out[6]);
  not not_7 (not_7_out, driver_15_out[5]);
  PullDown pulldown_7 (.out(out_28));
  assign out_9 = out_28 ? or_1_out : 8'bz;  // Driver driver_13
  PullDown pulldown_8 (.out(out_30));
  assign out_9 = out_30 ? not_4_out : 8'bz;  // Driver driver_14
  not not_8 (not_8_out, driver_15_out[4]);
  not not_9 (not_9_out, driver_15_out[3]);
  assign driver_15_out = and_5_out ? out_17 : 8'bz;  // Driver driver_15
  not not_10 (not_10_out, driver_15_out[2]);
  not not_11 (not_11_out, driver_15_out[1]);
  not not_12 (not_12_out, driver_15_out[0]);
  and and_11 (and_11_out, not_12_out, driver_15_out[1], not_10_out, not_9_out, not_8_out, not_7_out, not_6_out, not_5_out);
  and and_12 (and_12_out, driver_15_out[0], driver_15_out[1], not_10_out, not_9_out, not_8_out, not_7_out, not_6_out, not_5_out);
  and and_13 (and_13_out, not_12_out, not_11_out, driver_15_out[2], not_9_out, not_8_out, not_7_out, not_6_out, not_5_out);
  and and_14 (and_14_out, driver_15_out[0], driver_15_out[1], driver_15_out[2], not_9_out, not_8_out, not_7_out, not_6_out, not_5_out);
  and and_15 (and_15_out, not_12_out, not_11_out, not_10_out, driver_15_out[3], not_8_out, not_7_out, not_6_out, not_5_out);
  and and_16 (and_16_out, driver_15_out[0], not_11_out, not_10_out, driver_15_out[3], not_8_out, not_7_out, not_6_out, not_5_out);
  PullDown #(.Bits(8)) pulldown_9 (.out(driver_15_out));
  assign out_2 = and_13_out ? 1'b1 : 1'bz;  // Driver driver_16
  assign out_9 = and_13_out ? out_16 : 8'bz;  // Driver driver_17
  assign out_4 = and_16_out ? 1'b1 : 1'bz;  // Driver driver_18
  assign out_9 = and_16_out ? out_16 : 8'bz;  // Driver driver_19
  assign out_2 = and_11_out ? 1'b1 : 1'bz;  // Driver driver_20
  assign out_8 = and_11_out ? 1'b1 : 1'bz;  // Driver driver_21
  assign out_10 = and_11_out ? out_16 : 8'bz;  // Driver driver_22
  assign out_1 = and_12_out ? 1'b1 : 1'bz;  // Driver driver_23
  assign out_7 = and_12_out ? 1'b1 : 1'bz;  // Driver driver_24
  assign out_10 = and_12_out ? out_16 : 8'bz;  // Driver driver_25
  assign out_4 = and_14_out ? 1'b1 : 1'bz;  // Driver driver_26
  assign out_8 = and_14_out ? 1'b1 : 1'bz;  // Driver driver_27
  assign out_10 = and_14_out ? out_16 : 8'bz;  // Driver driver_28
  assign out_3 = and_15_out ? 1'b1 : 1'bz;  // Driver driver_29
  assign out_7 = and_15_out ? 1'b1 : 1'bz;  // Driver driver_30
  assign out_10 = and_15_out ? out_16 : 8'bz;  // Driver driver_31
  PullDown pulldown_10 (.out(out_12));
  PullDown pulldown_11 (.out(out_11));
  PullDown pulldown_12 (.out(out_13));
  CounterPreset #(.maxValue(256), .Bits(8), .isProgramCounter("true")) counterpreset_1 (
    .en(out_11), .C(clk), .dir(1'b0), .in(out_9), .ld(out_13), .clr(1'b0), .out(out_15));  // open: ovf
  not not_13 (not_13_out, driver_15_out[7]);
  not not_14 (not_14_out, driver_15_out[6]);
  not not_15 (not_15_out, driver_15_out[5]);
  not not_16 (not_16_out, driver_15_out[4]);
  not not_17 (not_17_out, driver_15_out[3]);
  not not_18 (not_18_out, driver_15_out[2]);
  not not_19 (not_19_out, driver_15_out[1]);
  not not_20 (not_20_out, driver_15_out[0]);
  and and_17 (and_17_out, not_20_out, not_19_out, driver_15_out[2], driver_15_out[3], not_16_out, not_15_out, not_14_out, not_13_out);
  and and_18 (and_18_out, driver_15_out[0], not_19_out, driver_15_out[2], driver_15_out[3], not_16_out, not_15_out, not_14_out, not_13_out);
  and and_19 (and_19_out, not_20_out, driver_15_out[1], driver_15_out[2], driver_15_out[3], not_16_out, not_15_out, not_14_out, not_13_out);
  Register #(.Bits(8)) AR (.D(out_9), .C(clk), .en(out_6), .Q(out_16));
  PullDown pulldown_13 (.out(out_6));
  PullDown pulldown_14 (.out(out_24));
  or or_2 (or_2_out, out_24, IC_ovf);
  assign out_22 = and_17_out ? 1'b1 : 1'bz;  // Driver driver_32
  assign out_8 = and_17_out ? 1'b1 : 1'bz;  // Driver driver_33
  assign out_10 = and_17_out ? out_16 : 8'bz;  // Driver driver_34
  assign out_21 = and_18_out ? 1'b1 : 1'bz;  // Driver driver_35
  assign out_7 = and_18_out ? 1'b1 : 1'bz;  // Driver driver_36
  assign out_10 = and_18_out ? out_16 : 8'bz;  // Driver driver_37
  assign out_22 = and_19_out ? 1'b1 : 1'bz;  // Driver driver_38
  assign out_9 = and_19_out ? out_16 : 8'bz;  // Driver driver_39
  PullDown #(.Bits(8)) pulldown_15 (.out(out_9));
  Counter #(.Bits(2)) IC (.en(1'b1), .C(clk), .clr(or_2_out), .out(out_18), .ovf(IC_ovf));
  Register #(.Bits(8)) IR (.D(out_9), .C(clk), .en(out_5), .Q(out_17));
  PullDown pulldown_16 (.out(out_5));
  PullDown #(.Bits(8)) pulldown_17 (.out(out_10));
  PullDown pulldown_18 (.out(out_7));
  not not_21 (not_21_out, driver_15_out[7]);
  PullDown pulldown_19 (.out(out_8));
  not not_22 (not_22_out, driver_15_out[6]);
  not not_23 (not_23_out, driver_15_out[5]);
  RAMSinglePort #(.AddrBits(8), .Bits(8)) ramsingleport_1 (.A(out_10), .str(out_7), .C(clk), .ld(out_8), .D(out_9));
  not not_24 (not_24_out, driver_15_out[4]);
  not not_25 (not_25_out, driver_15_out[3]);
  PullDown pulldown_20 (.out(out_14));
  ROM #(.AddrBits(8), .isProgramMemory("true"), .Bits(8)) rom_1 (.A(out_15), .sel(1'b1), .D(rom_1_d));
  // Probe on out_9
  not not_26 (not_26_out, driver_15_out[2]);
  not not_27 (not_27_out, driver_15_out[1]);
  assign out_9 = out_14 ? rom_1_d : 8'bz;  // Driver driver_40
  not not_28 (not_28_out, driver_15_out[0]);
  and and_20 (and_20_out, not_28_out, not_27_out, not_26_out, not_25_out, not_24_out, driver_15_out[5], not_22_out, not_21_out);
  and and_21 (and_21_out, driver_15_out[0], driver_15_out[1], not_26_out, not_25_out, not_24_out, driver_15_out[5], not_22_out, not_21_out);
  and and_22 (and_22_out, not_28_out, not_27_out, driver_15_out[2], not_25_out, not_24_out, driver_15_out[5], not_22_out, not_21_out);
  and and_23 (and_23_out, driver_15_out[0], driver_15_out[1], driver_15_out[2], driver_15_out[3], driver_15_out[4], driver_15_out[5], not_22_out, not_21_out);
  assign out_13 = and_20_out ? 1'b1 : 1'bz;  // Driver driver_41
  assign WJMP = and_20_out ? 1'b1 : 1'bz;  // Driver driver_42
  assign WJMPSTORE = and_20_out ? 1'b1 : 1'bz;  // Driver driver_43
  assign out_9 = and_20_out ? out_16 : 8'bz;  // Driver driver_44
  and and_24 (and_24_out, and_21_out, out_31);
  and and_25 (and_25_out, and_22_out, out_33[0]);
  assign out_12 = and_23_out ? 1'b1 : 1'bz;  // Driver driver_45
  assign out_13 = and_24_out ? 1'b1 : 1'bz;  // Driver driver_46
  assign WJMP = and_24_out ? 1'b1 : 1'bz;  // Driver driver_47
  assign WJMPSTORE = and_24_out ? 1'b1 : 1'bz;  // Driver driver_48
  assign out_9 = and_24_out ? out_16 : 8'bz;  // Driver driver_49
  assign out_13 = and_25_out ? 1'b1 : 1'bz;  // Driver driver_50
  assign WJMP = and_25_out ? 1'b1 : 1'bz;  // Driver driver_51
  assign WJMPSTORE = and_25_out ? 1'b1 : 1'bz;  // Driver driver_52
  assign out_9 = and_25_out ? out_16 : 8'bz;  // Driver driver_53
  Register #(.Bits(8)) REGOUT (.D(out_20), .C(clk), .en(OUT), .Q(REGOUT_q));
  PullDown pulldown_21 (.out(OUT));
  Seven_Seg seven_seg_1 (
    .a(rom_2_d_2[3]), .b(rom_2_d_2[2]), .c(rom_2_d_2[1]), .d(rom_2_d_2[0]), .e(rom_2_d[2]), .f(rom_2_d[1]),
    .g(rom_2_d[0]), .dp(1'b0));
  ROM #(.AddrBits(8), .Bits(8)) rom_2 (.A(REGOUT_q), .sel(1'b1), .D({rom_2_d[7], rom_2_d_2, rom_2_d[2:0]}));
  Seven_Seg seven_seg_2 (
    .a(rom_3_d_2[3]), .b(rom_3_d_2[2]), .c(rom_3_d_2[1]), .d(rom_3_d_2[0]), .e(rom_3_d[2]), .f(rom_3_d[1]),
    .g(rom_3_d[0]), .dp(1'b0));
  ROM #(.AddrBits(8), .Bits(8)) rom_3 (.A(REGOUT_q), .sel(1'b1), .D({rom_3_d[7], rom_3_d_2, rom_3_d[2:0]}));
  not not_29 (not_29_out, driver_15_out[7]);
  not not_30 (not_30_out, driver_15_out[6]);
  not not_31 (not_31_out, driver_15_out[5]);
  not not_32 (not_32_out, driver_15_out[4]);
  Seven_Seg seven_seg_3 (
    .a(rom_4_d_2[3]), .b(rom_4_d_2[2]), .c(rom_4_d_2[1]), .d(rom_4_d_2[0]), .e(rom_4_d[2]), .f(rom_4_d[1]),
    .g(rom_4_d[0]), .dp(1'b0));
  ROM #(.AddrBits(8), .Bits(8)) rom_4 (.A(REGOUT_q), .sel(1'b1), .D({rom_4_d[7], rom_4_d_2, rom_4_d[2:0]}));
  not not_33 (not_33_out, driver_15_out[3]);
  not not_34 (not_34_out, driver_15_out[2]);
  not not_35 (not_35_out, driver_15_out[1]);
  not not_36 (not_36_out, driver_15_out[0]);
  and and_26 (and_26_out, not_36_out, not_35_out, not_34_out, not_33_out, not_32_out, not_31_out, driver_15_out[6], not_29_out);
  and and_27 (and_27_out, not_36_out, not_35_out, not_34_out, not_33_out, not_32_out, not_31_out, not_30_out, driver_15_out[7]);
  assign out_26 = and_26_out ? 1'b1 : 1'bz;  // Driver driver_54
  assign out_4 = and_26_out ? 1'b1 : 1'bz;  // Driver driver_55
  assign out_3 = and_27_out ? 1'b1 : 1'bz;  // Driver driver_56
  assign OUT = and_27_out ? 1'b1 : 1'bz;  // Driver driver_57
  PullDown pulldown_22 (.out(out_1));
  VGA vga_1 ();  // open: R, G, B, H, V, C
  Register #(.Bits(8)) REGA (.D(out_9), .C(clk), .en(out_2), .Q(out_19));
  PullDown pulldown_23 (.out(out_2));
  assign out_9 = out_1 ? out_19 : 8'bz;  // Driver driver_58
  PullDown pulldown_24 (.out(out_3));
  PullDown pulldown_25 (.out(out_4));
  Register #(.Bits(8)) REGB (.D(out_9), .C(clk), .en(out_4), .Q(out_20));
  assign out_9 = out_3 ? out_20 : 8'bz;  // Driver driver_59
  PullDown pulldown_26 (.out(out_21));
  Register #(.Bits(8)) REGC (.D(out_9), .C(clk), .en(out_22), .Q(out_23));
  PullDown pulldown_27 (.out(out_22));
  assign out_9 = out_21 ? out_23 : 8'bz;  // Driver driver_60
  // Pins of 1 and 8 bits meet at out_33

  assign out_32 = out_26;
  assign out_34 = out_33;

  // Other names for the same wires on the sheet: ANDEN = out_27; AR[7:0] = out_16; AREAD = out_1; ARSTORE = out_6;
  //   ASTORE = out_2; BREAD = out_3; BSTORE = out_4; CLOCK = clk; CREAD = out_21; CRFLAG = out_31; ADDEN = out_26;
  //   CRSTORE = out_26; CSTORE = out_22; DBUS[7:0] = out_9; IC[1:0] = out_18; ICRESET = out_24; IR[7:0] = out_17;
  //   IRSTORE = out_5; MADDR[7:0] = out_10; MREAD = out_8; MSTORE = out_7; NANDEN = out_35; NOTEN = out_30;
  //   OREN = out_28; PC[7:0] = out_15; PCINC = out_11; PCRESET = out_12; PCSET = out_13; REGA[7:0] = out_19;
  //   REGB[7:0] = out_20; REGC[7:0] = out_23; ROMREAD = out_14; XOREN = out_29; ZRFLAG[7:0] = out_33

  // Notes on the sheet:
  //   clk: Hz: 50
  //   CARRY FLAG REGISTER
  //   ZERO FLAG
  //   FULL FLAG
  //   "Will jump" register
  //   Micro steps
  //   ADDER
  //   AND
  //   XOR
  //   NAND
  //   DECODE INSTRUCTION
  //   NAME
  //   DECODE INSTRUCTION
  //   ARGUMENT
  //   End of cycle
  //   OR
  //   NOT
  //   PROGRAM COUNTER
  //   2: IMA
  //   3: EXA
  //   4: LIA
  //   7: IMB
  //   8: EXB
  //   9: LIB
  //   ARGUMENT REGISTER
  //   INTERNAL COUNTER
  //   DATA BUS MONITOR
  //   INSTRUCTION REGISTER
  //   12: IMC
  //   13: EXC
  //   14: LIC
  //   RANDOM ACCESS MEMORY
  //   PROGRAM ROM
  //   rom_1 loads code.hex
  //   OUT
  //   63: HLT
  //   32: JMP
  //   35: JMC
  //   36: JMZ
  //   rom_2 loads seg_display_2.hex
  //   rom_3 loads seg_display_1.hex
  //   rom_4 loads seg_display_0.hex
  //   64: ADD
  //   128: OUT
  //   A REGISTER
  //   B REGISTER
  //   C REGISTER
endmodule
