// Digital circuit 8_bit_adder.dig as structural Verilog
module _8_bit_adder (
);

  one_full_bit_adder one_full_bit_adder_1 ();  // open: A_i, B_i, C_in, O_i, C_out
  one_full_bit_adder one_full_bit_adder_2 ();  // open: A_i, B_i, C_in, O_i, C_out
  one_full_bit_adder one_full_bit_adder_3 ();  // open: A_i, B_i, C_in, O_i, C_out
endmodule
