// Digital circuit computer_parts.dig as structural Verilog
module computer_parts (
  output out_1,
  output out_2,
  output out_3,
  output out_4,
  output out_5
);

  wire button_1_out, one_full_counter_2_out_old, one_full_counter_3_out_old, one_full_counter_4_out_old,
       one_full_counter_5_out_old, one_full_counter_6_out_old, one_full_counter_7_out_old,
       one_full_counter_8_out_old, pullup_1_out;
  wire [7:0] and_1_out, and_2_out, DBUS, not_1_out, or_1_out, PC_old, REGA, REGB, xor_1_out;

  one_full_counter one_full_counter_1 (
    .old(PC_old[6]), .\new (one_full_counter_2_out_old), .clock(button_1_out), .out(PC_old[7]));  // open: out_old
  one_full_counter one_full_counter_2 (
    .old(PC_old[5]), .\new (one_full_counter_3_out_old), .clock(button_1_out), .out(PC_old[6]),
    .out_old(one_full_counter_2_out_old));
  one_full_counter one_full_counter_3 (
    .old(PC_old[4]), .\new (one_full_counter_4_out_old), .clock(button_1_out), .out(PC_old[5]),
    .out_old(one_full_counter_3_out_old));
  assign and_1_out = REGA & REGB;  // And and_1, 8 bits wide
  assign xor_1_out = REGA ^ REGB;  // XOr xor_1, 8 bits wide
  assign and_2_out = REGA & REGB;  // And and_2, 8 bits wide
  assign DBUS = out_1 ? and_1_out : 8'bz;  // Driver driver_1
  assign DBUS = out_3 ? xor_1_out : 8'bz;  // Driver driver_2
  assign DBUS = out_5 ? and_2_out : 8'bz;  // Driver driver_3
  one_full_counter one_full_counter_4 (
    .old(PC_old[3]), .\new (one_full_counter_5_out_old), .clock(button_1_out), .out(PC_old[4]),
    .out_old(one_full_counter_4_out_old));
  PullDown pulldown_1 (.out(out_1));
  PullDown pulldown_2 (.out(out_3));
  PullDown pulldown_3 (.out(out_5));
  LED led_1 (.in(PC_old[7]));
  one_full_counter one_full_counter_5 (
    .old(PC_old[2]), .\new (one_full_counter_6_out_old), .clock(button_1_out), .out(PC_old[3]),
    .out_old(one_full_counter_5_out_old));
  LED led_2 (.in(PC_old[6]));
  LED led_3 (.in(PC_old[4]));
  LED led_4 (.in(PC_old[5]));
  assign or_1_out = REGA | REGB;  // Or or_1, 8 bits wide
  assign not_1_out = ~REGA;  // Not not_1, 8 bits wide
  one_full_counter one_full_counter_6 (
    .old(PC_old[1]), .\new (one_full_counter_7_out_old), .clock(button_1_out), .out(PC_old[2]),
    .out_old(one_full_counter_6_out_old));
  LED led_5 (.in(PC_old[3]));
  assign DBUS = out_2 ? or_1_out : 8'bz;  // Driver driver_4
  assign DBUS = out_4 ? not_1_out : 8'bz;  // Driver driver_5
  LED led_6 (.in(PC_old[2]));
  PullDown pulldown_4 (.out(out_2));
  PullDown pulldown_5 (.out(out_4));
  one_full_counter one_full_counter_7 (
    .old(PC_old[0]), .\new (one_full_counter_8_out_old), .clock(button_1_out), .out(PC_old[1]),
    .out_old(one_full_counter_7_out_old));
  LED led_7 (.in(PC_old[0]));
  LED led_8 (.in(PC_old[1]));
  Button button_1 (.out(button_1_out));
  one_full_counter one_full_counter_8 (
    .old(pullup_1_out), .\new (pullup_1_out), .clock(button_1_out), .out(PC_old[0]),
    .out_old(one_full_counter_8_out_old));
  PullUp pullup_1 (.out(pullup_1_out));

  // Other names for the same wires on the sheet: ANDEN = out_1; NANDEN = out_5; NOTEN = out_4; OREN = out_2;
  //   XOREN = out_3

  // Notes on the sheet:
  //   AND
  //   XOR
  //   NAND
  //   OR
  //   NOT
endmodule
