// Digital circuit one_full_bit_adder.dig as structural Verilog
module one_full_bit_adder (
  input  A_i,
  input  B_i,
  input  C_in,
  output O_i,
  output C_out
);

  wire and_1_out, and_2_out, xor_1_out;

  xor xor_1 (xor_1_out, A_i, B_i);
  xor xor_2 (O_i, xor_1_out, C_in);
  and and_1 (and_1_out, B_i, A_i);
  and and_2 (and_2_out, C_in, xor_1_out);
  or or_1 (C_out, and_1_out, and_2_out);
endmodule
