// Digital circuit one_full_counter.dig as structural Verilog
module one_full_counter (
  input  old,
  input  \new ,
  input  clock,
  output out,
  output out_old
);

  and and_1 (out_old, old, \new );
  JK_FF jk_ff_1 (.J(out_old), .C(clock), .K(out_old), .Q(out));  // open: nQ
endmodule
